// Logisim project MIPS.circ as structural Verilog: 1 circuit, main circuit main
module main (
);

  wire and_1_out, BNE, Branch, Clear, Clock, Exception, ExcOut, Jump, JumpRegister, multiplexer_4_out,
       not_1_out, Zero;
  wire [25:0] \decodificador_de_instrução_1_addr ;
  wire [29:0] imm32;
  wire [31:0] adder_1_out, EPC, LD1, multiplexer_1_out, multiplexer_2_out, multiplexer_3_out,
       multiplexer_5_out, multiplexer_6_out, PC_4, PC_q, undriven;

  Multiplexer #(.width(32), .enable("false")) multiplexer_1 (
    .in0(multiplexer_2_out), .out(multiplexer_1_out), .sel(Jump));  // open: in1
  Multiplexer #(.width(32), .enable("false")) multiplexer_2 (
    .in0(multiplexer_6_out), .in1(LD1), .out(multiplexer_2_out), .sel(JumpRegister));
  not not_1 (not_1_out, Zero);
  Multiplexer #(.width(32), .enable("false")) multiplexer_3 (
    .in0(multiplexer_1_out), .in1(32'h80000180), .out(multiplexer_3_out), .sel(Exception));
  Multiplexer #(.enable("false")) multiplexer_4 (.in0(Zero), .in1(not_1_out), .out(multiplexer_4_out), .sel(BNE));
  Multiplexer #(.width(32), .enable("false")) multiplexer_5 (
    .in0(multiplexer_3_out), .in1(EPC), .out(multiplexer_5_out), .sel(ExcOut));
  Multiplexer #(.width(32), .enable("false")) multiplexer_6 (
    .in0(PC_4), .in1(adder_1_out), .out(multiplexer_6_out), .sel(and_1_out));
  and and_1 (and_1_out, multiplexer_4_out, Branch);
  Register #(.width(32)) PC (.D(multiplexer_5_out), .en(1'b1), .Q(PC_q), .clk(Clock), .clr(Clear));
  Adder #(.width(32)) adder_1 (.a({imm32, 2'b00}), .b(PC_4), .out(adder_1_out));  // open: cin, cout
  Adder #(.width(32)) adder_2 (.a(32'h4), .b(PC_q), .out(PC_4));  // open: cin, cout
  mem_instr mem_instr_1 (.INPUT(undriven), .OUTPUT(PC_q));
  \decodificador_de_instrução  \decodificador_de_instrução_1  (
    .\Instrução (undriven), .addr(\decodificador_de_instrução_1_addr ));  // open: opcode, RS, RT, RD, shamt, funct, imm
endmodule
